# Fritzing sketch FritzingSeatalkDiagram (saved by Fritzing 0.9.10b)
perfboards: 2

parts:
  J4 = rounded female pin header, 12 pins [form="♀ (female rounded)"]  # not connected
  SeatalkIn = JST XH 3A Male [chip_label=? package=THT]  # not connected
  J26 = rounded female pin header, 3 pins [form="♀ (female rounded)"]
  J27 = rounded female pin header, 3 pins [form="♀ (female rounded)"]
  J28 = rounded female pin header, 12 pins [form="♀ (female rounded)"]
  BC237 = NPN-Transistor [package="TO92 [THT]"]  # not connected
  BC212 = PNP-Transistor [package="TO92 [THT]"]  # not connected
  R1 = Resistor [tolerance=±5% power=0.25 resistance=10k package=THT]  # not connected
  R2 = Resistor [tolerance=±5% power=0.25 resistance=2.2k package=THT]  # not connected
  J29 = rounded female pin header, 3 pins [form="♀ (female rounded)"]
  R3 = Resistor [tolerance=±5% power=0.25 resistance=6.8k package=THT]  # not connected
  R4 = Resistor [tolerance=±5% power=0.25 resistance=10k package=THT]  # not connected
  R5 = Resistor [tolerance=±5% power=0.25 resistance=3.9k package=THT]  # not connected
  J31 = rounded female pin header, 5 pins [form="♀ (female rounded)"]
  J32 = rounded female pin header, 5 pins [form="♀ (female rounded)"]
  J33 = rounded female pin header, 5 pins [form="♀ (female rounded)"]
  J30 = rounded female pin header, 3 pins [form="♀ (female rounded)"]
  J34 = rounded female pin header, 5 pins [form="♀ (female rounded)"]
  J35 = rounded female pin header, 5 pins [form="♀ (female rounded)"]
  RS232 = danny-orionrobots [chip_label=?]  # not connected

nets:
  N1: J26.pin2, J35.pin1
  N2: J26.pin3, J32.pin5
  N3: J27.pin1, J29.pin3
  N4: J27.pin2, J30.pin3, J35.pin5
  N5: J28.pin2, J31.pin5
  N6: J28.pin6, J33.pin1
  N7: J28.pin12, J30.pin1
  N8: J29.pin1, J31.pin1
  N9: J29.pin2, J34.pin1
  N10: J30.pin2, J34.pin5

custom parts:
  JST XH 3A Male: 2.54 Mm JST "XH" connector
